# Fritzing sketch greenhouse_v0.1.1 (saved by Fritzing 1.0.0rc)
breadboards: 1

parts:
  Arduino_NANO = Arduino Nano (Rev3.0)
  Moistur_ANA = Soil Moisture Sensor
  DHT11_DIG = Humidity and Temperature Sensor DHT11
  R1 = PHOTOCELL [package=photocell]  # not connected
  R2 = Temperature Sensor (Thermistor) [thermistor_type=NTC package=THT]  # not connected
  S1 = Pushbutton [package="[THT]"]  # not connected
  LED1 = LED - 3mm [color="Orange (612nm)" current=0.030A package="3 mm [THT]"]  # not connected
  J1 = screw terminal, 2 pins
  V1 = DC Power [voltage=12V part_number=alimentatore]  # not connected

nets:
  GND: Arduino_NANO.GND, Moistur_ANA.GND, DHT11_DIG.GND_1, J1.pin2
  N1: Arduino_NANO.VIN, J1.pin1
  VCC: Arduino_NANO.5V, Moistur_ANA.VCC, DHT11_DIG.Vcc

custom parts:
  Humidity and Temperature Sensor DHT11: Digital relative humidity & temperature sensor DHT11
