# Fritzing sketch greenhouse_v1.0.1 (saved by Fritzing 1.0.0rc)
breadboards: 1

parts:
  DHT11_DIG = Humidity and Temperature Sensor DHT11  # not connected
  R2 = Temperature Sensor (Thermistor) [thermistor_type=NTC package=THT]  # not connected
  PWR = LED - 3mm [color="Green (565nm)" current=0.030A package="3 mm [THT]"]
  V1 = DC Power [voltage=12V part_number=alimentatore]  # not connected
  S2 = Pushbutton [package="[THT]"]  # not connected
  YL-69 = FC-28 Soil Hygrometer Module - Probe  # not connected
  DS1 = DS18B20 1-Wire Temperature Sensor [part_number=DS18B20]
  Arduino_NANO1 = Arduino Nano (Rev3.0)
  Q2 = Basic FET N-Channel [package="TO220 [THT]"]  # not connected
  PUMP = LED - 3mm [color="Green (565nm)" current=0.030A package="3 mm [THT]"]
  HEAT = LED - 3mm [color="Green (565nm)" current=0.030A package="3 mm [THT]"]
  R6 = Resistor [tolerance=±5% power=0.25W resistance=220 package=THT]
  R7 = Resistor [tolerance=±5% power=0.25W resistance=220 package=THT]
  R8 = Resistor [tolerance=±5% power=0.25W resistance=220 package=THT]
  R9 = Resistor [tolerance=±5% power=0.25W resistance=4.7k package=THT]
  PHOTO_R1 = PHOTOCELL [package=photocell]
  pot_T = Rotary Potentiometer (Large) [maximum_resistance=5kΩ knob_status=50% power=0.5W package=THT]
  pot_H = Rotary Potentiometer (Large) [maximum_resistance=5kΩ knob_status=50% power=0.5W package=THT]
  pot_L = Rotary Potentiometer (Large) [maximum_resistance=5kΩ knob_status=50% power=0.5W package=THT]
  Q3 = npn-Powertransistor [package="TO220 [THT]"]
  YL-70 = FC-28 Soil Hygrometer Module
  R10 = Resistor [tolerance=±5% power=0.25W resistance=4.7k package=THT]
  RELAYS = screw terminal, 3 pins
  R11 = Resistor [tolerance=±5% power=0.25W resistance=4.7k package=THT]
  DS18B20 = screw terminal, 3 pins
  DHT11 = screw terminal, 3 pins
  BTN_LAMP = Pushbutton [package="[THT]"]
  BTN_WLK = Pushbutton [package="[THT]"]
  BTN_DSPL = Pushbutton [package="[THT]"]
  PROX_TANK = Pushbutton [package="[THT]"]
  LCD = screw terminal, 4 pins

nets:
  GND: PWR.cathode, DS1.GND, Arduino_NANO1.GND, PUMP.cathode, HEAT.cathode, R9.Pin_1, pot_T.leg1, pot_H.leg1, pot_L.leg1, Q3.emitter, DS18B20.pin3, DHT11.pin3, BTN_LAMP.Pin_1, BTN_LAMP.Pin_2, BTN_WLK.Pin_1, BTN_WLK.Pin_2, BTN_DSPL.Pin_1, BTN_DSPL.Pin_2, PROX_TANK.Pin_2, LCD.pin4
  N1: PWR.anode, R6.Pin_1
  5V: DS1.VDD, Arduino_NANO1.5V, PHOTO_R1.P$1, pot_T.leg2, pot_H.leg2, pot_L.leg2, YL-70.VCC, R11.Pin_0, DS18B20.pin1, DHT11.pin1, LCD.pin1
  N2: Arduino_NANO1.D2, PROX_TANK.Pin_3, PROX_TANK.Pin_4
  N3: Arduino_NANO1.D3, BTN_DSPL.Pin_3, BTN_DSPL.Pin_4
  N4: Arduino_NANO1.D4, BTN_WLK.Pin_3, BTN_WLK.Pin_4
  N5: Arduino_NANO1.D5, BTN_LAMP.Pin_3, BTN_LAMP.Pin_4
  N6: Arduino_NANO1.D6, DHT11.pin2
  N7: Arduino_NANO1.D7, R11.Pin_1, DS18B20.pin2
  N8: Arduino_NANO1.D8, RELAYS.pin3
  N9: Arduino_NANO1.D9, RELAYS.pin2
  N10: Arduino_NANO1.D10, RELAYS.pin1
  N11: Arduino_NANO1.D11/MOSI, R7.Pin_0
  N12: Arduino_NANO1.D12/MISO, R8.Pin_0
  N13: Arduino_NANO1.A7, R10.Pin_0
  N14: Arduino_NANO1.A6, YL-70.AO
  N15: Arduino_NANO1.A5, LCD.pin3
  N16: Arduino_NANO1.A4, LCD.pin2
  N17: Arduino_NANO1.A3, pot_L.wiper
  N18: Arduino_NANO1.A2, pot_H.wiper
  N19: Arduino_NANO1.A1, pot_T.wiper
  N20: Arduino_NANO1.A0, R9.Pin_0, PHOTO_R1.P$2
  N21: Arduino_NANO1.D13/SCK, R6.Pin_0
  N22: PUMP.anode, R7.Pin_1
  N23: HEAT.anode, R8.Pin_1
  N24: Q3.base, R10.Pin_1
  N25: Q3.collector, YL-70.GND

custom parts:
  Humidity and Temperature Sensor DHT11: Digital relative humidity & temperature sensor DHT11
  FC-28 Soil Hygrometer Module - Probe: The FC-28 is a soil hygrometer module that uses the Texas Instruments LM393 comparator chip to provide an analog measurement of soil humidity.
  FC-28 Soil Hygrometer Module: The FC-28 is a soil hygrometer module that uses the Texas Instruments LM393 comparator chip to provide an analog measurement of soil humidity. The digital output is high when soil moisture is over a certain threshold, as determined by adjusting the potentiometer.
